// Logisim project 8_bit_CPU.circ as structural Verilog: 3 circuits, main circuit main
module main (
  output [3:0] out_1,
  output [7:0] out_2,
  output [15:0] out_3
);

  wire button_1_out, button_2_out, button_3_out, button_4_out, clock_1_out, d_ff_1_q, d_ff_1_qn, d_ff_2_q,
       d_ff_2_qn, d_ff_3_q, d_ff_3_qn, d_ff_4_q, d_ff_4_qn, d_ff_5_q, d_ff_5_qn, d_ff_6_q, d_ff_6_qn,
       nand_1_out, not_1_out, register_8bit_3_borrow, register_8bit_3_carry, RESET_out, undriven_4,
       undriven_5;
  wire [7:0] undriven_2, undriven_3;
  wire [8:0] undriven;

  Button #(.press("passive")) button_1 (.out(button_1_out));
  not not_1 (not_1_out, button_1_out);
  ROM #(.addrWidth(9)) rom_1 (.addr(undriven));  // open: data
  nand nand_1 (nand_1_out, button_1_out, not_1_out);
  Clock clock_1 (.out(clock_1_out));
  Button RESET (.out(RESET_out));
  Button #(.press("passive")) button_2 (.out(button_2_out));
  Button #(.press("passive")) button_3 (.out(button_3_out));
  Button #(.press("passive")) button_4 (.out(button_4_out));
  register_8bit register_8bit_1 (
    .DATA(undriven_3), .NOT_WRITE(1'b1), .RESET(RESET_out), .INC(register_8bit_3_carry),
    .DEC(register_8bit_3_borrow), .Q(out_3[15:8]));  // open: CARRY, BORROW
  RAM ram_1 ();  // open: addr, we, oe, clk, din, dout
  ring_counter ring_counter_1 (.CLK(clock_1_out), .RESET(RESET_out), .Q(out_1));
  register_8bit register_8bit_2 (
    .DATA(8'h80), .NOT_WRITE(button_2_out), .RESET(RESET_out), .INC(button_3_out), .DEC(button_4_out),
    .Q(out_2));  // open: CARRY, BORROW
  register_8bit register_8bit_3 (
    .DATA(undriven_2), .NOT_WRITE(1'b1), .RESET(RESET_out), .INC(undriven_4), .DEC(1'b1), .Q(out_3[7:0]),
    .CARRY(register_8bit_3_carry), .BORROW(register_8bit_3_borrow));
  D_Flip_Flop d_ff_1 (.D(d_ff_1_qn), .Q(d_ff_1_q), .Qn(d_ff_1_qn), .reset(undriven_5));  // open: clk, preset
  D_Flip_Flop d_ff_2 (
    .D(d_ff_2_qn), .clk(d_ff_1_qn), .Q(d_ff_2_q), .Qn(d_ff_2_qn), .reset(undriven_5));  // open: preset
  D_Flip_Flop d_ff_3 (
    .D(d_ff_3_qn), .clk(d_ff_2_qn), .Q(d_ff_3_q), .Qn(d_ff_3_qn), .reset(undriven_5));  // open: preset
  D_Flip_Flop d_ff_4 (
    .D(d_ff_4_qn), .clk(d_ff_3_qn), .Q(d_ff_4_q), .Qn(d_ff_4_qn), .reset(undriven_5));  // open: preset
  D_Flip_Flop d_ff_5 (
    .D(d_ff_5_qn), .clk(d_ff_4_qn), .Q(d_ff_5_q), .Qn(d_ff_5_qn), .reset(undriven_5));  // open: preset
  D_Flip_Flop d_ff_6 (
    .D(d_ff_6_qn), .clk(d_ff_5_qn), .Q(d_ff_6_q), .Qn(d_ff_6_qn), .reset(undriven_5));  // open: preset
endmodule

module register_8bit (
  input  [7:0] DATA,
  input  NOT_WRITE,
  input  RESET,
  input  INC,
  input  DEC,
  output [7:0] Q,
  output CARRY,
  output BORROW
);

  wire n74193_1_pin4, n74193_1_pin5;

  _74193 #(.ShowInternalStructure("true")) u_74193_1 (
    .pin1(DATA[5]), .pin2(Q[5]), .pin3(Q[4]), .pin4(n74193_1_pin4), .pin5(n74193_1_pin5), .pin6(Q[6]),
    .pin7(Q[7]), .pin15(DATA[4]), .pin14(RESET), .pin13(BORROW), .pin12(CARRY), .pin11(NOT_WRITE),
    .pin10(DATA[6]), .pin9(DATA[7]));
  _74193 #(.ShowInternalStructure("true")) u_74193_2 (
    .pin1(DATA[1]), .pin2(Q[1]), .pin3(Q[0]), .pin4(DEC), .pin5(INC), .pin6(Q[2]), .pin7(Q[3]),
    .pin15(DATA[0]), .pin14(RESET), .pin13(n74193_1_pin4), .pin12(n74193_1_pin5), .pin11(NOT_WRITE),
    .pin10(DATA[2]), .pin9(DATA[3]));
endmodule

module ring_counter (
  input  CLK,
  input  RESET,
  output [3:0] Q
);

  wire nor_1_out, or_1_out, or_2_out;

  D_Flip_Flop d_ff_1 (.D(Q[0]), .clk(CLK), .Q(Q[3]), .preset(nor_1_out), .reset(RESET));  // open: Qn
  or or_1 (or_1_out, Q[3], Q[2]);
  D_Flip_Flop d_ff_2 (.D(Q[3]), .clk(CLK), .Q(Q[2]), .reset(RESET));  // open: Qn, preset
  nor nor_1 (nor_1_out, or_1_out, or_2_out);
  D_Flip_Flop d_ff_3 (.D(Q[2]), .clk(CLK), .Q(Q[1]), .reset(RESET));  // open: Qn, preset
  or or_2 (or_2_out, Q[1], Q[0]);
  D_Flip_Flop d_ff_4 (.D(Q[1]), .clk(CLK), .Q(Q[0]), .reset(RESET));  // open: Qn, preset
endmodule
